# Fritzing sketch WiringDiagram (saved by Fritzing 0.9.5d)
stripboards: 1

parts:
  M4 = Stepper Motor - Bipolar
  Pololu_A3 = Pololu A4988 [package=SO16]
  C3 = Electrolytic Capacitor [capacitance=10μF package="0605 [SMD, electrolytic]"]
  M5 = Stepper Motor - Bipolar
  Pololu_A4 = Pololu A4988 [package=SO16]
  C4 = Electrolytic Capacitor [capacitance=10μF package="0605 [SMD, electrolytic]"]
  HC-SR04_Sensor_1 = HC-SR04 Ultrasonic Distance Sensor
  Mod1 = ESP32 - CAM
  Mod2 = ESP32 - CAM
  M6 = RioRand LM2596
  J1 = Basic Servo
  J2 = Basic Servo
  BMS1 = BMS
  ESP1 = DIP - 42 pins
  LiPo1 = DIP - 6 pins [package=Battery]
  IC1 = DIP - 8 pins [chip_label=IC package="DIP (Dual Inline) [THT]"]
  IC2 = DIP - 8 pins [chip_label=IC package="DIP (Dual Inline) [THT]"]
  L298N1 = L298N DC motor driver

nets (from the breadboard view):
  N1: M4.A, Pololu_A3.2B
  N2: M4.C, Pololu_A3.2A
  N3: M4.B, Pololu_A3.1A
  N4: M4.D, Pololu_A3.1B
  N5: Pololu_A3.RESET, Pololu_A3.SLEEP
  N6: Pololu_A3.STEP, ESP1.GPIO08
  N7: Pololu_A3.DIR, ESP1.GPIO07
  GND: Pololu_A3.GND#8, Pololu_A4.GND#8, HC-SR04_Sensor_1.GND, Mod1.GND, Mod2.GND, M6.Pin_4, J1.gnd, J2.gnd, ESP1.GND
  VCC: Pololu_A3.VDD, Pololu_A4.VDD, HC-SR04_Sensor_1.VCC, Mod1.5V, Mod2.5V, M6.Pin_3, J1.vcc, J2.vcc, ESP1.5v0, L298N1.5V
  N8: Pololu_A3.GND#14, C3.-, Pololu_A4.GND#14, C4.-, M6.Pin_2, BMS1.Load_-, L298N1.GND
  N9: Pololu_A3.VMOT, C3.+, Pololu_A4.VMOT, C4.+, M6.Pin_1, BMS1.Load_+, L298N1.12V
  N10: M5.A, Pololu_A4.2B
  N11: M5.C, Pololu_A4.2A
  N12: M5.B, Pololu_A4.1A
  N13: M5.D, Pololu_A4.1B
  N14: Pololu_A4.RESET, Pololu_A4.SLEEP
  N15: Pololu_A4.STEP, ESP1.GPIO10
  N16: Pololu_A4.DIR, ESP1.GPIO09
  N17: HC-SR04_Sensor_1.TRIG, ESP1.GPIO13
  N18: HC-SR04_Sensor_1.ECHO, ESP1.GPIO12
  N19: J1.pulse, ESP1.GPIO37
  N20: J2.pulse, ESP1.GPIO38
  N21: BMS1.0V, LiPo1.V-, LiPo1.0V
  N22: BMS1.4.2V, LiPo1.4.2V
  N23: BMS1.8.4V, LiPo1.8.4V
  N24: BMS1.12.6V, LiPo1.V+, LiPo1.12.6V
  N25: ESP1.GPIO01, L298N1.ENB
  N26: ESP1.GPIO02, L298N1.IN4
  N27: ESP1.GPIO03, L298N1.IN3
  N28: ESP1.GPIO04, L298N1.IN2
  N29: ESP1.GPIO05, L298N1.IN1
  N30: ESP1.GPIO06, L298N1.ENA
  N31: IC1.red, L298N1.OUT2
  N32: IC1.black, L298N1.OUT1
  N33: IC2.red, L298N1.OUT3
  N34: IC2.black, L298N1.OUT4

custom parts:
  ESP32 - CAM: The ESP32-CAM has a very competitive small-size camera module that can operate independently as a minimum system with a footprint of only 27*40.5*4.5mm and a deep sleep current of up to 6mA.
  BMS: BMS for 3S battery
  DIP - 42 pins: ESP32-S2-DevKitM-1
  DIP - 6 pins: A LiPo 3S
  DIP - 8 pins: A DIP stand-in part for whatever IC you want. With 8 pins on a 300mil dual inline package (DIP) footprint.
  L298N DC motor driver: 2x DC motor driver with 78M05 positive voltage regulator (7..35 V) L298N: max 46 V, 2 A Set 5 V Enable jumper to enable 5 V regultor (needed for the L298N) and +5 V output at screw terminal or supply external +5 V at screw terminal Set ENA and/or ENB to +5 V to enable motor permanently or supply ENA and/or ENB with PWM signal IN1 and IN2 set rotation directory for motor A (OUT1/OUT2) IN2 and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
